# Fritzing sketch picow_tnpn_led1w (saved by Fritzing 0.9.3b)
breadboards: 1

parts:
  Mod1 = Raspberry Pi Pico W
  T1 = NPN-Transistor [part_number=S8050 package="TO92 [THT]"]
  R1 = Resistor [tolerance=±5% resistance=1k power=1 package=THT]
  LED1 = Super Flux LED blue [color=Blue]

nets:
  N1: Mod1.pin_3, Mod1.pin_8, Mod1.pin_13, Mod1.pin_18, Mod1.pin_23, Mod1.pin_28, Mod1.pin_33, Mod1.pin_38, T1.E
  N2: Mod1.pin_20, R1.Pin_0
  N3: T1.B, R1.Pin_1
  N4: T1.C, LED1.cathode

custom parts:
  Raspberry Pi Pico W: Raspberry Pi Pico W. Based around the RP2040 microcontroller the Pico W is a low cost microcontroller device bringing Raspberry Pi quality, cost, and easy of use to the microcontroller space. The areas marked KEEPOUT in pcb silkscreen should not have traces running through them to avoid shorts on a soldered in module!
