# Fritzing sketch test_tnpn_led1w (saved by Fritzing 0.9.3b)
breadboards: 1

parts:
  T1 = NPN-Transistor [part_number=2N2222A package="TO92 [THT]"]
  R1 = Resistor [tolerance=±5% resistance=1k package=THT]
  LED1 = Super Flux LED blue [color=Blue]
  3_7_volt = battery_holder_single_18650
  V1 = DC Power [voltage=4.8]
  S2 = Pushbutton [package=THT]  # not connected
  R2 = Resistor [tolerance=±5% resistance=10k package=THT]
  2_8_mA = Amperemeter
  100_-_150_mA = Amperemeter
  3_2_volt = Voltmeter
  R3 = Resistor [tolerance=±5% resistance=4.7 power=500mW package=THT]

nets:
  N1: T1.E, 3_7_volt.+#0, V1.V-
  N2: T1.B, R1.Pin_1, R2.Pin_0
  N3: T1.C, R3.Pin_1
  N4: LED1.cathode, 3_2_volt.Positive, R3.Pin_0
  N5: LED1.anode, 100_-_150_mA.Positive, 3_2_volt.Com
  N6: 3_7_volt.+#1, 2_8_mA.Positive
  N7: V1.V+, 100_-_150_mA.Com

custom parts:
  battery_holder_single_18650: single 18650 battery holder
  Amperemeter: A Standard Multimeter in Current mode
  Voltmeter: A Standard Multimeter in Current mode
